# Fritzing sketch ProjectFzz (saved by Fritzing 0.9.3b)

parts:
  Part1 = Arduino Pro Mini v13
  Part2 = Bluetooth HC-05 Macho
  RHT1 = Humidity and Temperature Sensor RHT03
  Repr_Sensor_Magnetico_(PullUp) = NPN-Transistor [package="TO92 [THT]"]

nets:
  GND: Part1.GND, Part2.GND
  VCC: Part1.VCC, Part2.VCC
  N1: Part1.A3, RHT1.Data-signal
  N2: Part1.D12/MISO, Repr_Sensor_Magnetico_(PullUp).C
  N3: Part1.D11_PWM/MOSI, Part2.RXD
  N4: Part1.D10_PWM/SS, Part2.TXD
  N5: RHT1.Vcc, Repr_Sensor_Magnetico_(PullUp).E
